// Logisim project my10.circ as structural Verilog: 14 circuits, main circuit main
module main (
);

  wire and_1_out, and_2_out, and_3_out, and_4_out, and_5_out, and_6_out, buffer_1_out, buffer_3_out,
       buffer_5_out, button_1_out, clock, comparator_1_eq, controlled_buffer_3_out, counter_1_carry,
       counter_2_carry, Ingame, key, keyboard_2_avail, lost, not_1_out, not_2_out, not_3_out, not_4_out,
       not_5_out, not_6_out, or_2_out, or_3_out, or_4_out, or_5_out, or_6_out, q, Restart, start, v, win,
       win_or_not_1_out_2, win_or_not_1_out_3, win_or_not_1_out_4;
  wire [1:0] keyboard_1_right;
  wire [2:0] go, move;
  wire [2:1] keyboard_1_up;
  wire [3:0] dozens, hundreds, units;
  wire [6:0] cp_1_askii, \input , keyboard_2_data, name_input;
  wire [7:0] adder_1_out, adder_2_out, counter_4_q, down_1_out_2, left_1_out_2, multiplexer_1_out, Pos,
       register_2_q, right_1_out_2, up_1_out_2;
  wire [27:0] screen_1_out_21, screen_1_out_25, screen_1_out_29, screen_1_out_33, screen_1_out_37,
       screen_1_out_41, screen_1_out_45, screen_1_out_49, screen_1_out_53, screen_1_out_57, screen_1_out_61,
       screen_1_out_65, screen_1_out_69, screen_1_out_73, screen_1_out_77, screen_1_out_81, screen_1_out_85,
       screen_1_out_89, screen_1_out_93, screen_1_out_97, screen_1_out_101, screen_1_out_105,
       screen_1_out_109, screen_1_out_113, screen_1_out_117, screen_1_out_121, screen_1_out_125,
       screen_1_out_129, screen_1_out_133, screen_1_out_137;
  wire [28:0] screen_1_out_20, screen_1_out_24, screen_1_out_28, screen_1_out_32, screen_1_out_36,
       screen_1_out_40, screen_1_out_44, screen_1_out_48, screen_1_out_52, screen_1_out_56, screen_1_out_60,
       screen_1_out_64, screen_1_out_68, screen_1_out_72, screen_1_out_76, screen_1_out_80, screen_1_out_84,
       screen_1_out_88, screen_1_out_92, screen_1_out_96, screen_1_out_100, screen_1_out_104,
       screen_1_out_108, screen_1_out_112, screen_1_out_116, screen_1_out_120, screen_1_out_124,
       screen_1_out_128, screen_1_out_132, screen_1_out_136;
  wire [29:0] key_1__1, key_1__2, key_1__3, key_1__4, key_1__5, key_1__6, key_1__7, key_1__8, key_1__9,
       key_1__10, key_1__11, key_1__12, key_1__13, key_1__14, key_1__15, key_1__16, key_1__17, key_1__18;
  wire [30:0] screen_1_out_22, screen_1_out_26, screen_1_out_30, screen_1_out_34, screen_1_out_38,
       screen_1_out_42, screen_1_out_46, screen_1_out_50, screen_1_out_54, screen_1_out_58, screen_1_out_62,
       screen_1_out_66, screen_1_out_70, screen_1_out_74, screen_1_out_78, screen_1_out_82, screen_1_out_86,
       screen_1_out_90, screen_1_out_94, screen_1_out_98, screen_1_out_102, screen_1_out_106,
       screen_1_out_110, screen_1_out_114, screen_1_out_118, screen_1_out_122, screen_1_out_126,
       screen_1_out_130, screen_1_out_134, screen_1_out_138, screen_1_out_140;
  wire [31:0] len_1_out_2, len_2_out_2, len_3_out_2, player_scheme_1_out_12, player_scheme_1_out_13,
       player_scheme_1_out_14, player_scheme_1_out_15, player_scheme_1_out_16, player_scheme_1_out_17,
       player_scheme_1_out_18, player_scheme_1_out_19, player_scheme_1_out_20, player_scheme_1_out_21,
       screen_1_out_18, screen_1_out_19, screen_1_out_23, screen_1_out_27, screen_1_out_31, screen_1_out_35,
       screen_1_out_39, screen_1_out_43, screen_1_out_47, screen_1_out_51, screen_1_out_55, screen_1_out_59,
       screen_1_out_63, screen_1_out_67, screen_1_out_71, screen_1_out_75, screen_1_out_79, screen_1_out_83,
       screen_1_out_87, screen_1_out_91, screen_1_out_95, screen_1_out_99, screen_1_out_103,
       screen_1_out_107, screen_1_out_111, screen_1_out_115, screen_1_out_119, screen_1_out_123,
       screen_1_out_127, screen_1_out_131, screen_1_out_135, screen_1_out_139;

  assign Pos = not_1_out ? 8'he1 : 8'bz;  // Controlled_Buffer controlled_buffer_1
  not not_1 (not_1_out, Ingame);
  // Probe on \input 
  keyboard keyboard_1 (
    .a(\input ), .Left(keyboard_1_right[1]), .Right(keyboard_1_right[0]), .Up(keyboard_1_up[1]),
    .Down(keyboard_1_up[2]), .Reset(Restart));
  len len_1 (.in_1(Pos), .out_2(len_1_out_2));
  Comparator comparator_1 (.a(Pos), .b(8'he1), .eq(comparator_1_eq));  // open: gt, lt
  // Probe on move
  assign move = {1'b0, keyboard_1_right} | {keyboard_1_up, keyboard_1_up[1]};  // OR_Gate or_1, 3 bits wide
  len len_2 (.in_1(adder_1_out), .out_2(len_2_out_2));
  Adder adder_1 (.a(8'hf0), .b(Pos), .out(adder_1_out));  // open: cin, cout
  player_scheme player_scheme_1 (
    .in_1(go), .out_12(player_scheme_1_out_12), .in_2(len_1_out_2), .out_13(player_scheme_1_out_13),
    .in_3(len_1_out_2), .out_14(player_scheme_1_out_14), .in_4(len_1_out_2), .out_15(player_scheme_1_out_15),
    .in_5(len_1_out_2), .out_16(player_scheme_1_out_16), .in_6(len_1_out_2), .out_17(player_scheme_1_out_17),
    .in_7(len_1_out_2), .out_18(player_scheme_1_out_18), .in_8(len_1_out_2), .out_19(player_scheme_1_out_19),
    .in_9(len_1_out_2), .out_20(player_scheme_1_out_20), .in_10(len_1_out_2),
    .out_21(player_scheme_1_out_21), .in_11(len_1_out_2));
  len len_3 (.in_1(adder_2_out), .out_2(len_3_out_2));
  Adder adder_2 (.a(Pos), .b(8'h10), .out(adder_2_out));  // open: cin, cout
  not not_2 (not_2_out, Ingame);
  Register #(.width(1)) register_1 (.D(and_1_out), .en(1'b1), .Q(Ingame), .clk(or_2_out));  // open: clr
  and and_1 (and_1_out, not_2_out, comparator_1_eq);
  or or_2 (or_2_out, Restart, and_2_out);
  and and_2 (and_2_out, clock, ~Ingame);  // AND_Gate
  or or_3 (or_3_out, move[0], move[1], move[2]);
  Register register_2 (.D(Pos), .en(1'b1), .Q(register_2_q), .clk(clock));  // open: clr
  screen screen_1 (
    .in_2(win), .in_3(lost), .in_6(len_2_out_2), .out_19(screen_1_out_19), .out_23(screen_1_out_23),
    .out_27(screen_1_out_27), .out_31(screen_1_out_31), .out_35(screen_1_out_35), .out_39(screen_1_out_39),
    .out_43(screen_1_out_43), .out_47(screen_1_out_47), .out_51(screen_1_out_51), .out_55(screen_1_out_55),
    .in_7(player_scheme_1_out_12), .out_59(screen_1_out_59), .in_8(player_scheme_1_out_13),
    .out_63(screen_1_out_63), .in_9(player_scheme_1_out_14), .out_67(screen_1_out_67),
    .in_10(player_scheme_1_out_15), .out_71(screen_1_out_71), .in_11(player_scheme_1_out_16),
    .out_75(screen_1_out_75), .in_12(player_scheme_1_out_17), .out_79(screen_1_out_79),
    .in_13(player_scheme_1_out_18), .out_83(screen_1_out_83), .in_14(player_scheme_1_out_19),
    .out_87(screen_1_out_87), .in_15(player_scheme_1_out_20), .out_91(screen_1_out_91),
    .in_16(player_scheme_1_out_21), .out_95(screen_1_out_95), .out_99(screen_1_out_99),
    .out_103(screen_1_out_103), .out_107(screen_1_out_107), .out_111(screen_1_out_111),
    .out_115(screen_1_out_115), .out_119(screen_1_out_119), .out_123(screen_1_out_123),
    .out_127(screen_1_out_127), .out_131(screen_1_out_131), .out_135(screen_1_out_135), .in_17(len_3_out_2),
    .out_20(screen_1_out_20), .out_24(screen_1_out_24), .out_28(screen_1_out_28), .out_32(screen_1_out_32),
    .out_36(screen_1_out_36), .out_40(screen_1_out_40), .out_44(screen_1_out_44), .out_48(screen_1_out_48),
    .out_52(screen_1_out_52), .out_56(screen_1_out_56), .out_60(screen_1_out_60), .out_64(screen_1_out_64),
    .out_68(screen_1_out_68), .out_72(screen_1_out_72), .out_76(screen_1_out_76), .out_80(screen_1_out_80),
    .out_84(screen_1_out_84), .out_88(screen_1_out_88), .out_92(screen_1_out_92), .out_96(screen_1_out_96),
    .out_100(screen_1_out_100), .out_104(screen_1_out_104), .out_108(screen_1_out_108),
    .out_112(screen_1_out_112), .out_116(screen_1_out_116), .out_120(screen_1_out_120),
    .out_124(screen_1_out_124), .out_128(screen_1_out_128), .out_132(screen_1_out_132),
    .out_136(screen_1_out_136), .out_21(screen_1_out_21), .out_25(screen_1_out_25), .out_29(screen_1_out_29),
    .out_33(screen_1_out_33), .out_37(screen_1_out_37), .out_41(screen_1_out_41), .out_45(screen_1_out_45),
    .out_49(screen_1_out_49), .out_53(screen_1_out_53), .out_57(screen_1_out_57), .out_61(screen_1_out_61),
    .out_65(screen_1_out_65), .out_69(screen_1_out_69), .out_73(screen_1_out_73), .out_77(screen_1_out_77),
    .out_81(screen_1_out_81), .out_85(screen_1_out_85), .out_89(screen_1_out_89), .out_93(screen_1_out_93),
    .out_97(screen_1_out_97), .out_101(screen_1_out_101), .out_105(screen_1_out_105),
    .out_109(screen_1_out_109), .out_113(screen_1_out_113), .out_117(screen_1_out_117),
    .out_125(screen_1_out_125), .out_129(screen_1_out_129), .out_133(screen_1_out_133),
    .out_137(screen_1_out_137), .out_121(screen_1_out_121), .in_4(v), .out_18(screen_1_out_18),
    .out_139(screen_1_out_139), .in_1(q), .in_5(key), .out_22(screen_1_out_22), .out_26(screen_1_out_26),
    .out_30(screen_1_out_30), .out_34(screen_1_out_34), .out_38(screen_1_out_38), .out_42(screen_1_out_42),
    .out_46(screen_1_out_46), .out_50(screen_1_out_50), .out_54(screen_1_out_54), .out_58(screen_1_out_58),
    .out_62(screen_1_out_62), .out_66(screen_1_out_66), .out_70(screen_1_out_70), .out_74(screen_1_out_74),
    .out_78(screen_1_out_78), .out_82(screen_1_out_82), .out_86(screen_1_out_86), .out_90(screen_1_out_90),
    .out_94(screen_1_out_94), .out_98(screen_1_out_98), .out_102(screen_1_out_102),
    .out_106(screen_1_out_106), .out_110(screen_1_out_110), .out_114(screen_1_out_114),
    .out_118(screen_1_out_118), .out_122(screen_1_out_122), .out_126(screen_1_out_126),
    .out_130(screen_1_out_130), .out_134(screen_1_out_134), .out_138(screen_1_out_138),
    .out_140(screen_1_out_140));
  Counter #(.width(4), .max('ha), .ongoal("load")) counter_1 (
    .count(1'b1), .Q(units), .carry(counter_1_carry), .clk(and_3_out), .clr(buffer_1_out));  // open: load, D
  and and_3 (and_3_out, or_3_out, clock);
  buf buffer_1 (buffer_1_out, Restart);
  left left_1 (.in_1(register_2_q), .out_2(left_1_out_2));
  right right_1 (.in_1(register_2_q), .out_2(right_1_out_2));
  up up_1 (.in_1(register_2_q), .out_2(up_1_out_2));
  buf buffer_2 (buffer_1_out, counter_1_carry);
  buf buffer_3 (buffer_3_out, Restart);
  down down_1 (.in_1(register_2_q), .out_2(down_1_out_2));
  Multiplexer #(.select(3), .width(8), .enable("false")) multiplexer_1 (
    .in0(register_2_q), .in1(left_1_out_2), .in2(right_1_out_2), .in3(up_1_out_2), .in4(down_1_out_2),
    .out(multiplexer_1_out), .sel(move));  // open: in5, in6, in7
  Counter #(.width(4), .max('ha), .ongoal("load")) counter_2 (
    .count(buffer_1_out), .Q(dozens), .carry(counter_2_carry), .clk(counter_1_carry), .clr(buffer_3_out));  // open: load, D
  buf buffer_4 (buffer_3_out, counter_2_carry);
  assign Pos = Ingame ? multiplexer_1_out : 8'bz;  // Controlled_Buffer controlled_buffer_2
  Counter #(.width(4), .max('h9)) counter_3 (
    .count(buffer_3_out), .Q(hundreds), .clk(counter_2_carry), .clr(buffer_5_out));  // open: load, D, carry
  buf buffer_5 (buffer_5_out, Restart);
  win_or_not win_or_not_1 (
    .in_1(Pos), .out_2(win_or_not_1_out_2), .out_3(win_or_not_1_out_3), .out_4(win_or_not_1_out_4),
    .out_5(v), .out_6(q));
  and and_4 (and_4_out, not_4_out, win_or_not_1_out_4);
  key key_1 (
    .in_1(key), ._1(key_1__1), ._2(key_1__2), ._3(key_1__3), ._4(key_1__4), ._5(key_1__5), ._6(key_1__6),
    ._7(key_1__7), ._8(key_1__8), ._9(key_1__9), ._10(key_1__10), ._11(key_1__11), ._12(key_1__12),
    ._13(key_1__13), ._14(key_1__14), ._15(key_1__15), ._16(key_1__16), ._17(key_1__17), ._18(key_1__18));
  DotMatrix #(.inputtype("row"), .matrixcols(30), .matrixrows(18)) dotmatrix_1 (
    .row0(key_1__1), .row1(key_1__2), .row2(key_1__3), .row3(key_1__4), .row4(key_1__5), .row5(key_1__6),
    .row6(key_1__7), .row7(key_1__8), .row8(key_1__9), .row9(key_1__10), .row10(key_1__11),
    .row11(key_1__12), .row12(key_1__13), .row13(key_1__14), .row14(key_1__15), .row15(key_1__16),
    .row16(key_1__17), .row17(key_1__18));
  DotMatrix #(.inputtype("row"), .matrixcols(32), .matrixrows(32)) dotmatrix_2 (
    .row0(screen_1_out_18), .row1(screen_1_out_19), .row2(screen_1_out_23), .row3(screen_1_out_27),
    .row4(screen_1_out_31), .row5(screen_1_out_35), .row6(screen_1_out_39), .row7(screen_1_out_43),
    .row8(screen_1_out_47), .row9(screen_1_out_51), .row10(screen_1_out_55), .row11(screen_1_out_59),
    .row12(screen_1_out_63), .row13(screen_1_out_67), .row14(screen_1_out_71), .row15(screen_1_out_75),
    .row16(screen_1_out_79), .row17(screen_1_out_83), .row18(screen_1_out_87), .row19(screen_1_out_91),
    .row20(screen_1_out_95), .row21(screen_1_out_99), .row22(screen_1_out_103), .row23(screen_1_out_107),
    .row24(screen_1_out_111), .row25(screen_1_out_115), .row26(screen_1_out_119), .row27(screen_1_out_123),
    .row28(screen_1_out_127), .row29(screen_1_out_131), .row30(screen_1_out_135), .row31(screen_1_out_139));
  DotMatrix #(.inputtype("row"), .matrixcols(28), .matrixrows(30)) dotmatrix_3 (
    .row0(screen_1_out_21), .row1(screen_1_out_25), .row2(screen_1_out_29), .row3(screen_1_out_33),
    .row4(screen_1_out_37), .row5(screen_1_out_41), .row6(screen_1_out_45), .row7(screen_1_out_49),
    .row8(screen_1_out_53), .row9(screen_1_out_57), .row10(screen_1_out_61), .row11(screen_1_out_65),
    .row12(screen_1_out_69), .row13(screen_1_out_73), .row14(screen_1_out_77), .row15(screen_1_out_81),
    .row16(screen_1_out_85), .row17(screen_1_out_89), .row18(screen_1_out_93), .row19(screen_1_out_97),
    .row20(screen_1_out_101), .row21(screen_1_out_105), .row22(screen_1_out_109), .row23(screen_1_out_113),
    .row24(screen_1_out_117), .row25(screen_1_out_121), .row26(screen_1_out_125), .row27(screen_1_out_129),
    .row28(screen_1_out_133), .row29(screen_1_out_137));
  DotMatrix #(.inputtype("row"), .matrixcols(29), .matrixrows(30)) dotmatrix_4 (
    .row0(screen_1_out_20), .row1(screen_1_out_24), .row2(screen_1_out_28), .row3(screen_1_out_32),
    .row4(screen_1_out_36), .row5(screen_1_out_40), .row6(screen_1_out_44), .row7(screen_1_out_48),
    .row8(screen_1_out_52), .row9(screen_1_out_56), .row10(screen_1_out_60), .row11(screen_1_out_64),
    .row12(screen_1_out_68), .row13(screen_1_out_72), .row14(screen_1_out_76), .row15(screen_1_out_80),
    .row16(screen_1_out_84), .row17(screen_1_out_88), .row18(screen_1_out_92), .row19(screen_1_out_96),
    .row20(screen_1_out_100), .row21(screen_1_out_104), .row22(screen_1_out_108), .row23(screen_1_out_112),
    .row24(screen_1_out_116), .row25(screen_1_out_120), .row26(screen_1_out_124), .row27(screen_1_out_128),
    .row28(screen_1_out_132), .row29(screen_1_out_136));
  DotMatrix #(.matrixcols(31), .matrixrows(31)) dotmatrix_5 (
    .col0(screen_1_out_22), .col1(screen_1_out_26), .col2(screen_1_out_30), .col3(screen_1_out_34),
    .col4(screen_1_out_38), .col5(screen_1_out_42), .col6(screen_1_out_46), .col7(screen_1_out_50),
    .col8(screen_1_out_54), .col9(screen_1_out_58), .col10(screen_1_out_62), .col11(screen_1_out_66),
    .col12(screen_1_out_70), .col13(screen_1_out_74), .col14(screen_1_out_78), .col15(screen_1_out_82),
    .col16(screen_1_out_86), .col17(screen_1_out_90), .col18(screen_1_out_94), .col19(screen_1_out_98),
    .col20(screen_1_out_102), .col21(screen_1_out_106), .col22(screen_1_out_110), .col23(screen_1_out_114),
    .col24(screen_1_out_118), .col25(screen_1_out_122), .col26(screen_1_out_126), .col27(screen_1_out_130),
    .col28(screen_1_out_134), .col29(screen_1_out_138), .col30(screen_1_out_140));
  not not_3 (not_3_out, lost);
  not not_4 (not_4_out, key);
  Register #(.width(1)) register_3 (.D(not_4_out), .en(1'b1), .Q(key), .clk(and_4_out), .clr(Restart));
  Clock clock_1 (.out(clock));
  Keyboard keyboard_2 (.clk(clock), .avail(keyboard_2_avail), .data(keyboard_2_data));  // open: re, clr
  or or_4 (or_4_out, move[0], move[1], move[2]);
  Register #(.width(1)) register_4 (.D(not_3_out), .en(1'b1), .Q(lost), .clk(win_or_not_1_out_3), .clr(Restart));
  not not_5 (not_5_out, win);
  and and_5 (and_5_out, win_or_not_1_out_2, key);
  assign controlled_buffer_3_out = not_6_out ? keyboard_2_avail : 1'bz;  // Controlled_Buffer controlled_buffer_3
  not not_6 (not_6_out, start);
  Counter counter_4 (
    .count(controlled_buffer_3_out), .Q(counter_4_q), .clk(controlled_buffer_3_out), .clr(button_1_out));  // open: load, D, carry
  Button button_1 (.out(button_1_out));
  and and_6 (and_6_out, or_4_out, clock);
  Register #(.width(1)) register_5 (.D(not_5_out), .en(1'b1), .Q(win), .clk(and_5_out), .clr(Restart));
  assign \input  = start ? keyboard_2_data : 7'bz;  // Controlled_Buffer controlled_buffer_4
  assign name_input = not_6_out ? keyboard_2_data : 7'bz;  // Controlled_Buffer controlled_buffer_5
  Comparator comparator_2 (.a(counter_4_q), .b(8'h5), .eq(start));  // open: gt, lt
  // Probe on go
  Register #(.width(3)) register_6 (.D(move), .en(1'b1), .Q(go), .clk(and_6_out), .clr(Restart));
  TTY #(.rows(1), .cols(6)) tty_1 (.data(name_input), .clk(or_5_out));  // open: we, clr
  or or_5 (or_5_out, name_input[0], name_input[1], name_input[2], name_input[3], name_input[4], name_input[5], name_input[6]);
  CP cp_1 (.ASKII(cp_1_askii));  // open: Name, Score, in_3
  or or_6 (or_6_out, cp_1_askii[0], cp_1_askii[1], cp_1_askii[2], cp_1_askii[3], cp_1_askii[4], cp_1_askii[5], cp_1_askii[6]);
  TTY #(.rows(5), .cols(6)) tty_2 (.data(cp_1_askii), .clk(or_6_out));  // open: we, clr
  Hex_Digit_Display hex_digit_display_1 (.value(dozens));  // open: dp
  Hex_Digit_Display hex_digit_display_2 (.value(hundreds));  // open: dp
  Hex_Digit_Display hex_digit_display_3 (.value(units));  // open: dp

  // Notes on the sheet:
  //   buffer_1 drives only 1 and floats otherwise
  //   buffer_2 drives only 1 and floats otherwise
  //   buffer_3 drives only 1 and floats otherwise
  //   buffer_4 drives only 1 and floats otherwise
  //   buffer_5 drives only 1 and floats otherwise
  //   Steps taken:
  //   Firstly enter your 5-character name
endmodule

module len (
  input  [7:0] in_1,
  output [31:0] out_2
);

  wire [7:0] adder_1_out, adder_2_out;

  Adder adder_1 (.a(in_1), .b({8{1'b1}}), .out(adder_1_out));  // open: cin, cout
  Adder adder_2 (.a(in_1), .b(8'h1), .out(adder_2_out));  // open: cin, cout
  ROM #(.dataWidth(1)) rom_1 (.addr(adder_1_out), .data(out_2[10]));  // open: sel
  ROM #(.dataWidth(1)) rom_2 (.addr(in_1), .data(out_2[20]));  // open: sel
  ROM #(.dataWidth(1)) rom_3 (.addr(adder_2_out), .data(out_2[29]));  // open: sel

  assign {out_2[31:30], out_2[28:21], out_2[19:11], out_2[9:0]} = {2'b11, {8{out_2[29]}}, {9{out_2[20]}}, {8{out_2[10]}}, 2'b11};

  // Notes on the sheet:
  //   contents of rom_1 (hex, n*v repeats v):
  //   17*1 0 0 0 1 0 0 0 1 6*0 1 1 0 1 0 1 0 1 0 0 0 4*1 0 1 1 0 1 0 1 0 1 1 1 4*0 1 0 1 1 0 1 0 1 0 0 0 1
  //   0 0 1 0 1 0 1 1 0 1 0 1 1 1 0 4*1 0 1 0 1 1 0 1 0 0 0 1 0 1 4*0 4*1 0 1 1 1 0 1 0 1 0 1 1 0 0 0 1 1
  //   0 0 0 1 0 1 0 1 0 0 1 1 1 0 1 1 0 1 0 1 0 1 0 1 1 0 1 0 0 0 1 1 0 1 0 1 4*0 1 0 1 0 4*1 0 1 0 6*1 0
  //   1 0 0 0 1 1 0 1 0 1 0 1 0 0 0 4*1 0 1 1 0 1 0 1 0 1 0 1 4*0 1 0 1 1 0 1 0 0 0 1 0 1 0 0 1 0 0 0 8*1
  //   0 8*1
  //   contents of rom_2 (hex, n*v repeats v):
  //   17*1 0 0 0 1 0 0 0 1 6*0 1 1 0 1 0 1 0 1 0 0 0 4*1 0 1 1 0 1 0 1 0 1 1 1 4*0 1 0 1 1 0 1 0 1 0 0 0 1
  //   0 0 1 0 1 0 1 1 0 1 0 1 1 1 0 4*1 0 1 0 1 1 0 1 0 0 0 1 0 1 4*0 4*1 0 1 1 1 0 1 0 1 0 1 1 0 0 0 1 1
  //   0 0 0 1 0 1 0 1 0 0 1 1 1 0 1 1 0 1 0 1 0 1 0 1 1 0 1 0 0 0 1 1 0 1 0 1 4*0 1 0 1 0 4*1 0 1 0 6*1 0
  //   1 0 0 0 1 1 0 1 0 1 0 1 0 0 0 4*1 0 1 1 0 1 0 1 0 1 0 1 4*0 1 0 1 1 0 1 0 0 0 1 0 1 0 0 1 0 0 0 8*1
  //   0 8*1
  //   contents of rom_3 (hex, n*v repeats v):
  //   17*1 0 0 0 1 0 0 0 1 6*0 1 1 0 1 0 1 0 1 0 0 0 4*1 0 1 1 0 1 0 1 0 1 1 1 4*0 1 0 1 1 0 1 0 1 0 0 0 1
  //   0 0 1 0 1 0 1 1 0 1 0 1 1 1 0 4*1 0 1 0 1 1 0 1 0 0 0 1 0 1 4*0 4*1 0 1 1 1 0 1 0 1 0 1 1 0 0 0 1 1
  //   0 0 0 1 0 1 0 1 0 0 1 1 1 0 1 1 0 1 0 1 0 1 0 1 1 0 1 0 0 0 1 1 0 1 0 1 4*0 1 0 1 0 4*1 0 1 0 6*1 0
  //   1 0 0 0 1 1 0 1 0 1 0 1 0 0 0 4*1 0 1 1 0 1 0 1 0 1 0 1 4*0 1 0 1 1 0 1 0 0 0 1 0 1 0 0 1 0 0 0 8*1
  //   0 8*1
endmodule

module right (
  input  [7:0] in_1,
  output [7:0] out_2
);

  wire not_1_out, rom_1_data;
  wire [7:0] adder_1_out;

  Adder adder_1 (.a(8'h1), .b(in_1), .out(adder_1_out));  // open: cin, cout
  ROM #(.dataWidth(1)) rom_1 (.addr(adder_1_out), .data(rom_1_data));  // open: sel
  not not_1 (not_1_out, rom_1_data);
  Multiplexer #(.width(8)) multiplexer_1 (.in0(in_1), .in1(adder_1_out), .out(out_2), .sel(not_1_out));  // open: en

  // Notes on the sheet:
  //   contents of rom_1 (hex, n*v repeats v):
  //   17*1 0 0 0 1 0 0 0 1 6*0 1 1 0 1 0 1 0 1 0 0 0 4*1 0 1 1 0 1 0 1 0 1 1 1 4*0 1 0 1 1 0 1 0 1 0 0 0 1
  //   0 0 1 0 1 0 1 1 0 1 0 1 1 1 0 4*1 0 1 0 1 1 0 1 0 0 0 1 0 1 4*0 4*1 0 1 1 1 0 1 0 1 0 1 1 0 0 0 1 1
  //   0 0 0 1 0 1 0 1 0 0 1 1 1 0 1 1 0 1 0 1 0 1 0 1 1 0 1 0 0 0 1 1 0 1 0 1 4*0 1 0 1 0 4*1 0 1 0 6*1 0
  //   1 0 0 0 1 1 0 1 0 1 0 1 0 0 0 4*1 0 1 1 0 1 0 1 0 1 0 1 4*0 1 0 1 1 0 1 0 0 0 1 0 1 0 0 1 0 0 0 8*1
  //   0 8*1
endmodule

module left (
  input  [7:0] in_1,
  output [7:0] out_2
);

  wire not_1_out, rom_1_data;
  wire [7:0] adder_1_out;

  Adder adder_1 (.a({8{1'b1}}), .b(in_1), .out(adder_1_out));  // open: cin, cout
  ROM #(.dataWidth(1)) rom_1 (.addr(adder_1_out), .data(rom_1_data));  // open: sel
  not not_1 (not_1_out, rom_1_data);
  Multiplexer #(.width(8)) multiplexer_1 (.in0(in_1), .in1(adder_1_out), .out(out_2), .sel(not_1_out));  // open: en

  // Notes on the sheet:
  //   contents of rom_1 (hex, n*v repeats v):
  //   17*1 0 0 0 1 0 0 0 1 6*0 1 1 0 1 0 1 0 1 0 0 0 4*1 0 1 1 0 1 0 1 0 1 1 1 4*0 1 0 1 1 0 1 0 1 0 0 0 1
  //   0 0 1 0 1 0 1 1 0 1 0 1 1 1 0 4*1 0 1 0 1 1 0 1 0 0 0 1 0 1 4*0 4*1 0 1 1 1 0 1 0 1 0 1 1 0 0 0 1 1
  //   0 0 0 1 0 1 0 1 0 0 1 1 1 0 1 1 0 1 0 1 0 1 0 1 1 0 1 0 0 0 1 1 0 1 0 1 4*0 1 0 1 0 4*1 0 1 0 6*1 0
  //   1 0 0 0 1 1 0 1 0 1 0 1 0 0 0 4*1 0 1 1 0 1 0 1 0 1 0 1 4*0 1 0 1 1 0 1 0 0 0 1 0 1 0 0 1 0 0 0 8*1
  //   0 8*1
endmodule

module down (
  input  [7:0] in_1,
  output [7:0] out_2
);

  wire not_1_out, rom_1_data;
  wire [7:0] adder_1_out;

  Adder adder_1 (.a(8'h10), .b(in_1), .out(adder_1_out));  // open: cin, cout
  ROM #(.dataWidth(1)) rom_1 (.addr(adder_1_out), .data(rom_1_data));  // open: sel
  not not_1 (not_1_out, rom_1_data);
  Multiplexer #(.width(8)) multiplexer_1 (.in0(in_1), .in1(adder_1_out), .out(out_2), .sel(not_1_out));  // open: en

  // Notes on the sheet:
  //   contents of rom_1 (hex, n*v repeats v):
  //   17*1 0 0 0 1 0 0 0 1 6*0 1 1 0 1 0 1 0 1 0 0 0 4*1 0 1 1 0 1 0 1 0 1 1 1 4*0 1 0 1 1 0 1 0 1 0 0 0 1
  //   0 0 1 0 1 0 1 1 0 1 0 1 1 1 0 4*1 0 1 0 1 1 0 1 0 0 0 1 0 1 4*0 4*1 0 1 1 1 0 1 0 1 0 1 1 0 0 0 1 1
  //   0 0 0 1 0 1 0 1 0 0 1 1 1 0 1 1 0 1 0 1 0 1 0 1 1 0 1 0 0 0 1 1 0 1 0 1 4*0 1 0 1 0 4*1 0 1 0 6*1 0
  //   1 0 0 0 1 1 0 1 0 1 0 1 0 0 0 4*1 0 1 1 0 1 0 1 0 1 0 1 4*0 1 0 1 1 0 1 0 0 0 1 0 1 0 0 1 0 0 0 8*1
  //   0 8*1
endmodule

module up (
  input  [7:0] in_1,
  output [7:0] out_2
);

  wire not_1_out, rom_1_data;
  wire [7:0] adder_1_out;

  Adder adder_1 (.a(8'hf0), .b(in_1), .out(adder_1_out));  // open: cin, cout
  ROM #(.dataWidth(1)) rom_1 (.addr(adder_1_out), .data(rom_1_data));  // open: sel
  not not_1 (not_1_out, rom_1_data);
  Multiplexer #(.width(8)) multiplexer_1 (.in0(in_1), .in1(adder_1_out), .out(out_2), .sel(not_1_out));  // open: en

  // Notes on the sheet:
  //   contents of rom_1 (hex, n*v repeats v):
  //   17*1 0 0 0 1 0 0 0 1 6*0 1 1 0 1 0 1 0 1 0 0 0 4*1 0 1 1 0 1 0 1 0 1 1 1 4*0 1 0 1 1 0 1 0 1 0 0 0 1
  //   0 0 1 0 1 0 1 1 0 1 0 1 1 1 0 4*1 0 1 0 1 1 0 1 0 0 0 1 0 1 4*0 4*1 0 1 1 1 0 1 0 1 0 1 1 0 0 0 1 1
  //   0 0 0 1 0 1 0 1 0 0 1 1 1 0 1 1 0 1 0 1 0 1 0 1 1 0 1 0 0 0 1 1 0 1 0 1 4*0 1 0 1 0 4*1 0 1 0 6*1 0
  //   1 0 0 0 1 1 0 1 0 1 0 1 0 0 0 4*1 0 1 1 0 1 0 1 0 1 0 1 4*0 1 0 1 1 0 1 0 0 0 1 0 1 0 0 1 0 0 0 8*1
  //   0 8*1
endmodule

module win_or_not (
  input  [7:0] in_1,
  output out_2,
  output out_3,
  output out_4,
  output out_5,
  output out_6
);

  wire comparator_2_eq, comparator_3_eq, comparator_4_eq;

  Comparator comparator_1 (.a(in_1), .b(8'hf7), .eq(out_2));  // open: gt, lt
  Comparator comparator_2 (.a(in_1), .b(8'hc5), .eq(comparator_2_eq));  // open: gt, lt
  Comparator comparator_3 (.a(in_1), .b(8'hba), .eq(comparator_3_eq));  // open: gt, lt
  Comparator comparator_4 (.a(in_1), .b(8'ha8), .eq(comparator_4_eq));  // open: gt, lt
  Comparator comparator_5 (.a(in_1), .b(8'h5e), .eq(out_4));  // open: gt, lt
  Comparator comparator_6 (.a(in_1), .b(8'he7), .eq(out_5));  // open: gt, lt
  Comparator comparator_7 (.a(in_1), .b(8'h4e), .eq(out_6));  // open: gt, lt
  or or_1 (out_3, comparator_2_eq, comparator_3_eq, comparator_4_eq);

  // Other names for the same wires on the sheet: V[7:0] = in_1
endmodule

module keyboard (
  input  [6:0] a,
  output Left,
  output Right,
  output Up,
  output Down,
  output Reset
);

  Comparator #(.width(7)) comparator_1 (.a(a), .b(7'b1100001), .eq(Left));  // open: gt, lt
  Comparator #(.width(7)) comparator_2 (.a(a), .b(7'b1100100), .eq(Right));  // open: gt, lt
  Comparator #(.width(7)) comparator_3 (.a(a), .b(7'b1110111), .eq(Up));  // open: gt, lt
  Comparator #(.width(7)) comparator_4 (.a(a), .b(7'b1110011), .eq(Down));  // open: gt, lt
  Comparator #(.width(7)) comparator_5 (.a(a), .b(7'b0100000), .eq(Reset));  // open: gt, lt

  // Notes on the sheet:
  //   d
  //   w
  //   s
endmodule

module player_scheme (
  input  [2:0] in_1,
  input  [31:0] in_2,
  input  [31:0] in_3,
  input  [31:0] in_4,
  input  [31:0] in_5,
  input  [31:0] in_6,
  input  [31:0] in_7,
  input  [31:0] in_8,
  input  [31:0] in_9,
  input  [31:0] in_10,
  input  [31:0] in_11,
  output [31:0] out_12,
  output [31:0] out_13,
  output [31:0] out_14,
  output [31:0] out_15,
  output [31:0] out_16,
  output [31:0] out_17,
  output [31:0] out_18,
  output [31:0] out_19,
  output [31:0] out_20,
  output [31:0] out_21
);

  wire [29:0] multiplexer_1_out, multiplexer_2_out, multiplexer_3_out, multiplexer_4_out, multiplexer_5_out,
       multiplexer_6_out, multiplexer_7_out, multiplexer_8_out, multiplexer_9_out, multiplexer_10_out;

  Multiplexer #(.select(3), .width(30), .enable("false")) multiplexer_1 (
    .in0(30'h80400), .in1(30'hd0400), .in2(30'h82c00), .in3(30'h80400), .in4(30'h9e400),
    .out(multiplexer_1_out), .sel(in_1));  // open: in5, in6, in7
  Multiplexer #(.select(3), .width(30), .enable("false")) multiplexer_2 (
    .in0(30'h52800), .in1(30'h9800), .in2(30'h64000), .in3(30'h52800), .in4(30'hbf400),
    .out(multiplexer_2_out), .sel(in_1));  // open: in5, in6, in7
  Multiplexer #(.select(3), .width(30), .enable("false")) multiplexer_3 (
    .in0(30'h52800), .in1(30'h6a000), .in2(30'h15800), .in3(30'h52800), .in4(30'h3f000),
    .out(multiplexer_3_out), .sel(in_1));  // open: in5, in6, in7
  Multiplexer #(.select(3), .width(30), .enable("false")) multiplexer_4 (
    .in0(30'h2d000), .in1(30'hf5800), .in2(30'h6bc00), .in3(30'h2d000), .in4(30'h9e400),
    .out(multiplexer_4_out), .sel(in_1));  // open: in5, in6, in7
  Multiplexer #(.select(3), .width(30), .enable("false")) multiplexer_5 (
    .in0(30'h1e000), .in1(30'hfe000), .in2(30'h1fc00), .in3(30'h1e000), .in4(30'h6d800),
    .out(multiplexer_5_out), .sel(in_1));  // open: in5, in6, in7
  Multiplexer #(.select(3), .width(30), .enable("false")) multiplexer_6 (
    .in0(30'h6d800), .in1(30'hfe000), .in2(30'h1fc00), .in3(30'h6d800), .in4(30'h1e000),
    .out(multiplexer_6_out), .sel(in_1));  // open: in5, in6, in7
  Multiplexer #(.select(3), .width(30), .enable("false")) multiplexer_7 (
    .in0(30'h9e400), .in1(30'hf5800), .in2(30'h6bc00), .in3(30'h9e400), .in4(30'h2d000),
    .out(multiplexer_7_out), .sel(in_1));  // open: in5, in6, in7
  Multiplexer #(.select(3), .width(30), .enable("false")) multiplexer_8 (
    .in0(30'h3f000), .in1(30'h6a000), .in2(30'h15800), .in3(30'h3f000), .in4(30'h52800),
    .out(multiplexer_8_out), .sel(in_1));  // open: in5, in6, in7
  Multiplexer #(.select(3), .width(30), .enable("false")) multiplexer_9 (
    .in0(30'hbf400), .in1(30'h9800), .in2(30'h64000), .in3(30'hbf400), .in4(30'h52800),
    .out(multiplexer_9_out), .sel(in_1));  // open: in5, in6, in7
  Multiplexer #(.select(3), .width(30), .enable("false")) multiplexer_10 (
    .in0(30'h9e400), .in1(30'hd0400), .in2(30'h82c00), .in3(30'h9e400), .in4(30'h80400),
    .out(multiplexer_10_out), .sel(in_1));  // open: in5, in6, in7
  assign out_12[30:1] = multiplexer_1_out | in_2[30:1];  // OR_Gate or_1, 30 bits wide
  assign out_13[30:1] = multiplexer_2_out | in_3[30:1];  // OR_Gate or_2, 30 bits wide
  assign out_14[30:1] = multiplexer_3_out | in_4[30:1];  // OR_Gate or_3, 30 bits wide
  assign out_15[30:1] = multiplexer_4_out | in_5[30:1];  // OR_Gate or_4, 30 bits wide
  assign out_16[30:1] = multiplexer_5_out | in_6[30:1];  // OR_Gate or_5, 30 bits wide
  assign out_17[30:1] = multiplexer_6_out | in_7[30:1];  // OR_Gate or_6, 30 bits wide
  assign out_18[30:1] = multiplexer_7_out | in_8[30:1];  // OR_Gate or_7, 30 bits wide
  assign out_19[30:1] = multiplexer_8_out | in_9[30:1];  // OR_Gate or_8, 30 bits wide
  assign out_20[30:1] = multiplexer_9_out | in_10[30:1];  // OR_Gate or_9, 30 bits wide
  assign out_21[30:1] = multiplexer_10_out | in_11[30:1];  // OR_Gate or_10, 30 bits wide

  assign {out_12[31], out_12[0]} = 2'b11;
  assign {out_13[31], out_13[0]} = 2'b11;
  assign {out_14[31], out_14[0]} = 2'b11;
  assign {out_15[31], out_15[0]} = 2'b11;
  assign {out_16[31], out_16[0]} = 2'b11;
  assign {out_17[31], out_17[0]} = 2'b11;
  assign {out_18[31], out_18[0]} = 2'b11;
  assign {out_19[31], out_19[0]} = 2'b11;
  assign {out_20[31], out_20[0]} = 2'b11;
  assign {out_21[31], out_21[0]} = 2'b11;

  // Other names for the same wires on the sheet: vec_adr[2:0] = in_1
endmodule

module key (
  input  in_1,
  output [29:0] _1,
  output [29:0] _2,
  output [29:0] _3,
  output [29:0] _4,
  output [29:0] _5,
  output [29:0] _6,
  output [29:0] _7,
  output [29:0] _8,
  output [29:0] _9,
  output [29:0] _10,
  output [29:0] _11,
  output [29:0] _12,
  output [29:0] _13,
  output [29:0] _14,
  output [29:0] _15,
  output [29:0] _16,
  output [29:0] _17,
  output [29:0] _18
);

  Multiplexer #(.width(30)) multiplexer_1 (.in0(30'h12e88b9c), .in1(30'h12e880), .out(_2), .sel(in_1));  // open: en
  Multiplexer #(.width(30)) multiplexer_2 (.in0(30'h14888ca2), .in1(30'h148880), .out(_3), .sel(in_1));  // open: en
  Multiplexer #(.width(30)) multiplexer_3 (.in0(30'h148d88a2), .in1(30'h148d80), .out(_4), .sel(in_1));  // open: en
  Multiplexer #(.width(30)) multiplexer_4 (.in0(30'h18e708a2), .in1(30'h18e700), .out(_5), .sel(in_1));  // open: en
  Multiplexer #(.width(30)) multiplexer_5 (.in0(30'h148208a2), .in1(30'h148200), .out(_6), .sel(in_1));  // open: en
  Multiplexer #(.width(30)) multiplexer_6 (.in0(30'h148208a2), .in1(30'h148200), .out(_7), .sel(in_1));  // open: en
  Multiplexer #(.width(30)) multiplexer_7 (.in0(30'h12e2089c), .in1(30'h12e200), .out(_8), .sel(in_1));  // open: en

  assign _1 = {30{1'b0}};
  assign _9 = {30{1'b0}};
  assign _10 = {30{1'b0}};
  assign _11 = 30'h1e722b02;
  assign _12 = 30'h10da2c82;
  assign _13 = 30'h108a2882;
  assign _14 = 30'h1c8a289e;
  assign _15 = 30'h108a28b2;
  assign _16 = 30'h10db68b2;
  assign _17 = 30'h1071c89e;
  assign _18 = {30{1'b0}};

  // Other names for the same wires on the sheet: vec_adr = in_1
endmodule

module screen (
  input  in_1,
  input  in_2,
  input  in_3,
  input  in_4,
  input  in_5,
  input  [31:0] in_6,
  input  [31:0] in_7,
  input  [31:0] in_8,
  input  [31:0] in_9,
  input  [31:0] in_10,
  input  [31:0] in_11,
  input  [31:0] in_12,
  input  [31:0] in_13,
  input  [31:0] in_14,
  input  [31:0] in_15,
  input  [31:0] in_16,
  input  [31:0] in_17,
  output [31:0] out_18,
  output [31:0] out_19,
  output [28:0] out_20,
  output [27:0] out_21,
  output [30:0] out_22,
  output [31:0] out_23,
  output [28:0] out_24,
  output [27:0] out_25,
  output [30:0] out_26,
  output [31:0] out_27,
  output [28:0] out_28,
  output [27:0] out_29,
  output [30:0] out_30,
  output [31:0] out_31,
  output [28:0] out_32,
  output [27:0] out_33,
  output [30:0] out_34,
  output [31:0] out_35,
  output [28:0] out_36,
  output [27:0] out_37,
  output [30:0] out_38,
  output [31:0] out_39,
  output [28:0] out_40,
  output [27:0] out_41,
  output [30:0] out_42,
  output [31:0] out_43,
  output [28:0] out_44,
  output [27:0] out_45,
  output [30:0] out_46,
  output [31:0] out_47,
  output [28:0] out_48,
  output [27:0] out_49,
  output [30:0] out_50,
  output [31:0] out_51,
  output [28:0] out_52,
  output [27:0] out_53,
  output [30:0] out_54,
  output [31:0] out_55,
  output [28:0] out_56,
  output [27:0] out_57,
  output [30:0] out_58,
  output [31:0] out_59,
  output [28:0] out_60,
  output [27:0] out_61,
  output [30:0] out_62,
  output [31:0] out_63,
  output [28:0] out_64,
  output [27:0] out_65,
  output [30:0] out_66,
  output [31:0] out_67,
  output [28:0] out_68,
  output [27:0] out_69,
  output [30:0] out_70,
  output [31:0] out_71,
  output [28:0] out_72,
  output [27:0] out_73,
  output [30:0] out_74,
  output [31:0] out_75,
  output [28:0] out_76,
  output [27:0] out_77,
  output [30:0] out_78,
  output [31:0] out_79,
  output [28:0] out_80,
  output [27:0] out_81,
  output [30:0] out_82,
  output [31:0] out_83,
  output [28:0] out_84,
  output [27:0] out_85,
  output [30:0] out_86,
  output [31:0] out_87,
  output [28:0] out_88,
  output [27:0] out_89,
  output [30:0] out_90,
  output [31:0] out_91,
  output [28:0] out_92,
  output [27:0] out_93,
  output [30:0] out_94,
  output [31:0] out_95,
  output [28:0] out_96,
  output [27:0] out_97,
  output [30:0] out_98,
  output [31:0] out_99,
  output [28:0] out_100,
  output [27:0] out_101,
  output [30:0] out_102,
  output [31:0] out_103,
  output [28:0] out_104,
  output [27:0] out_105,
  output [30:0] out_106,
  output [31:0] out_107,
  output [28:0] out_108,
  output [27:0] out_109,
  output [30:0] out_110,
  output [31:0] out_111,
  output [28:0] out_112,
  output [27:0] out_113,
  output [30:0] out_114,
  output [31:0] out_115,
  output [28:0] out_116,
  output [27:0] out_117,
  output [30:0] out_118,
  output [31:0] out_119,
  output [28:0] out_120,
  output [27:0] out_121,
  output [30:0] out_122,
  output [31:0] out_123,
  output [28:0] out_124,
  output [27:0] out_125,
  output [30:0] out_126,
  output [31:0] out_127,
  output [28:0] out_128,
  output [27:0] out_129,
  output [30:0] out_130,
  output [31:0] out_131,
  output [28:0] out_132,
  output [27:0] out_133,
  output [30:0] out_134,
  output [31:0] out_135,
  output [28:0] out_136,
  output [27:0] out_137,
  output [30:0] out_138,
  output [31:0] out_139,
  output [30:0] out_140
);

  wire door, key, undriven, vec_adr;
  wire [30:0] multiplexer_135_out, multiplexer_136_out, multiplexer_137_out, multiplexer_138_out,
       multiplexer_139_out, multiplexer_140_out, multiplexer_141_out, multiplexer_142_out,
       multiplexer_143_out;
  wire [31:0] help_me_1_out_3, help_me_1_out_4, help_me_2_out_3, help_me_2_out_4, help_me_3_out_3,
       help_me_3_out_4, help_me_4_out_3, help_me_4_out_4, help_me_5_out_3, help_me_5_out_4, help_me_6_out_3,
       help_me_6_out_4, help_me_7_out_3, help_me_7_out_4, help_me_8_out_3, help_me_8_out_4, help_me_9_out_3,
       help_me_9_out_4, help_me_10_out_3, help_me_10_out_4, help_me_11_out_3, help_me_11_out_4,
       help_me_12_out_3, help_me_12_out_4, help_me_13_out_3, help_me_13_out_4, help_me_14_out_3,
       help_me_14_out_4, help_me_15_out_3, help_me_15_out_4, help_me_16_out_3, help_me_16_out_4,
       help_me_17_out_3, help_me_17_out_4, help_me_18_out_3, help_me_18_out_4, help_me_19_out_3,
       help_me_19_out_4, help_me_20_out_3, help_me_20_out_4, help_me_21_out_3, help_me_21_out_4,
       help_me_22_out_3, help_me_22_out_4, help_me_23_out_3, help_me_23_out_4, help_me_24_out_3,
       help_me_24_out_4, help_me_25_out_3, help_me_25_out_4, help_me_26_out_3, help_me_26_out_4,
       help_me_27_out_3, help_me_27_out_4, help_me_28_out_3, help_me_28_out_4, multiplexer_1_out,
       multiplexer_2_out, multiplexer_3_out, multiplexer_4_out, multiplexer_5_out, multiplexer_6_out,
       multiplexer_7_out, multiplexer_8_out, multiplexer_9_out, multiplexer_10_out, multiplexer_11_out,
       multiplexer_12_out, multiplexer_13_out, multiplexer_14_out, multiplexer_15_out, multiplexer_16_out,
       multiplexer_17_out, multiplexer_18_out, multiplexer_19_out, multiplexer_20_out, multiplexer_21_out,
       multiplexer_22_out, multiplexer_23_out, multiplexer_24_out, multiplexer_25_out, multiplexer_26_out,
       multiplexer_27_out, multiplexer_28_out, multiplexer_29_out, multiplexer_30_out, multiplexer_31_out,
       multiplexer_32_out, multiplexer_33_out, multiplexer_34_out, multiplexer_35_out, multiplexer_36_out,
       multiplexer_37_out, multiplexer_38_out, multiplexer_39_out, multiplexer_40_out, multiplexer_41_out,
       multiplexer_42_out, multiplexer_43_out, multiplexer_44_out, multiplexer_45_out, multiplexer_46_out;

  and and_1 (key, in_1, ~in_5);  // AND_Gate
  and and_2 (vec_adr, in_4, ~in_5);  // AND_Gate
  and and_3 (door, in_4, in_5);
  Multiplexer #(.width(32)) multiplexer_1 (
    .in0(in_17), .in1(32'hffefffff), .out(multiplexer_1_out), .sel(door));  // open: en
  Multiplexer #(.width(32)) multiplexer_2 (
    .in0(in_17), .in1(32'hffed97ff), .out(multiplexer_2_out), .sel(door));  // open: en
  Multiplexer #(.width(32)) multiplexer_3 (
    .in0(in_17), .in1(32'hffea97ff), .out(multiplexer_3_out), .sel(door));  // open: en
  Multiplexer #(.width(32)) multiplexer_4 (
    .in0(in_17), .in1(32'hffe917ff), .out(multiplexer_4_out), .sel(door));  // open: en
  Multiplexer #(.width(32)) multiplexer_5 (
    .in0(in_17), .in1(32'hffeea7ff), .out(multiplexer_5_out), .sel(door));  // open: en
  Multiplexer #(.width(32)) multiplexer_6 (
    .in0(in_17), .in1(32'hffe847ff), .out(multiplexer_6_out), .sel(door));  // open: en
  Multiplexer #(.width(32)) multiplexer_7 (
    .in0(in_17), .in1(32'hffe8a7ff), .out(multiplexer_7_out), .sel(door));  // open: en
  Multiplexer #(.width(32)) multiplexer_8 (
    .in0(in_17), .in1(32'hffef17ff), .out(multiplexer_8_out), .sel(door));  // open: en
  Multiplexer #(.width(32)) multiplexer_9 (
    .in0(in_17), .in1(32'hffe807ff), .out(multiplexer_9_out), .sel(door));  // open: en
  Multiplexer #(.width(32)) multiplexer_10 (
    .in0(multiplexer_1_out), .in1(32'hffe007ff), .out(multiplexer_10_out), .sel(vec_adr));  // open: en
  Multiplexer #(.width(32)) multiplexer_11 (
    .in0(multiplexer_2_out), .in1(32'hffe187ff), .out(multiplexer_11_out), .sel(vec_adr));  // open: en
  Multiplexer #(.width(32)) multiplexer_12 (
    .in0(multiplexer_3_out), .in1(32'hffe247ff), .out(multiplexer_12_out), .sel(vec_adr));  // open: en
  Multiplexer #(.width(32)) multiplexer_13 (
    .in0(multiplexer_4_out), .in1(32'hffe7e7ff), .out(multiplexer_13_out), .sel(vec_adr));  // open: en
  Multiplexer #(.width(32)) multiplexer_14 (
    .in0(multiplexer_5_out), .in1(32'hffe427ff), .out(multiplexer_14_out), .sel(vec_adr));  // open: en
  Multiplexer #(.width(32)) multiplexer_15 (
    .in0(multiplexer_6_out), .in1(32'hffe527ff), .out(multiplexer_15_out), .sel(vec_adr));  // open: en
  Multiplexer #(.width(32)) multiplexer_16 (
    .in0(multiplexer_7_out), .in1(32'hffe427ff), .out(multiplexer_16_out), .sel(vec_adr));  // open: en
  Multiplexer #(.width(32)) multiplexer_17 (
    .in0(multiplexer_8_out), .in1(32'hffe7e7ff), .out(multiplexer_17_out), .sel(vec_adr));  // open: en
  Multiplexer #(.width(32)) multiplexer_18 (
    .in0(multiplexer_9_out), .in1(32'hffe007ff), .out(multiplexer_18_out), .sel(vec_adr));  // open: en
  Multiplexer #(.width(32)) multiplexer_19 (
    .in0(in_6), .in1(help_me_1_out_3), .out(multiplexer_19_out), .sel(in_2));  // open: en
  Multiplexer #(.width(32)) multiplexer_20 (
    .in0(in_6), .in1(help_me_2_out_3), .out(multiplexer_20_out), .sel(in_2));  // open: en
  Multiplexer #(.width(32)) multiplexer_21 (
    .in0(in_6), .in1(help_me_3_out_3), .out(multiplexer_21_out), .sel(in_2));  // open: en
  Multiplexer #(.width(32)) multiplexer_22 (
    .in0(in_6), .in1(help_me_4_out_3), .out(multiplexer_22_out), .sel(in_2));  // open: en
  Multiplexer #(.width(32)) multiplexer_23 (
    .in0(in_6), .in1(help_me_5_out_3), .out(multiplexer_23_out), .sel(in_2));  // open: en
  Multiplexer #(.width(32)) multiplexer_24 (
    .in0(in_6), .in1(help_me_6_out_3), .out(multiplexer_24_out), .sel(in_2));  // open: en
  Multiplexer #(.width(32)) multiplexer_25 (
    .in0(in_6), .in1(help_me_7_out_3), .out(multiplexer_25_out), .sel(in_2));  // open: en
  Multiplexer #(.width(32)) multiplexer_26 (
    .in0(in_6), .in1(help_me_8_out_3), .out(multiplexer_26_out), .sel(in_2));  // open: en
  Multiplexer #(.width(32)) multiplexer_27 (
    .in0(in_6), .in1(help_me_9_out_3), .out(multiplexer_27_out), .sel(in_2));  // open: en
  Multiplexer #(.width(32)) multiplexer_28 (
    .in0(in_7), .in1(help_me_10_out_3), .out(multiplexer_28_out), .sel(in_2));  // open: en
  Multiplexer #(.width(32)) multiplexer_29 (
    .in0(in_8), .in1(help_me_11_out_3), .out(multiplexer_29_out), .sel(in_2));  // open: en
  Multiplexer #(.width(32)) multiplexer_30 (
    .in0(in_9), .in1(help_me_12_out_3), .out(multiplexer_30_out), .sel(in_2));  // open: en
  Multiplexer #(.width(32)) multiplexer_31 (
    .in0(in_10), .in1(help_me_13_out_3), .out(multiplexer_31_out), .sel(in_2));  // open: en
  Multiplexer #(.width(32)) multiplexer_32 (
    .in0(in_11), .in1(help_me_14_out_3), .out(multiplexer_32_out), .sel(in_2));  // open: en
  Multiplexer #(.width(32)) multiplexer_33 (
    .in0(in_12), .in1(help_me_15_out_3), .out(multiplexer_33_out), .sel(in_2));  // open: en
  Multiplexer #(.width(32)) multiplexer_34 (
    .in0(in_13), .in1(help_me_16_out_3), .out(multiplexer_34_out), .sel(in_2));  // open: en
  Multiplexer #(.width(32)) multiplexer_35 (
    .in0(in_14), .in1(help_me_17_out_3), .out(multiplexer_35_out), .sel(in_2));  // open: en
  Multiplexer #(.width(32)) multiplexer_36 (
    .in0(in_15), .in1(help_me_18_out_3), .out(multiplexer_36_out), .sel(in_2));  // open: en
  Multiplexer #(.width(32)) multiplexer_37 (
    .in0(in_16), .in1(help_me_19_out_3), .out(multiplexer_37_out), .sel(in_2));  // open: en
  Multiplexer #(.width(32)) multiplexer_38 (
    .in0(multiplexer_10_out), .in1(help_me_20_out_3), .out(multiplexer_38_out), .sel(in_2));  // open: en
  Multiplexer #(.width(32)) multiplexer_39 (
    .in0(multiplexer_11_out), .in1(help_me_21_out_3), .out(multiplexer_39_out), .sel(in_2));  // open: en
  Multiplexer #(.width(32)) multiplexer_40 (
    .in0(multiplexer_12_out), .in1(help_me_22_out_3), .out(multiplexer_40_out), .sel(in_2));  // open: en
  Multiplexer #(.width(32)) multiplexer_41 (
    .in0(multiplexer_13_out), .in1(help_me_23_out_3), .out(multiplexer_41_out), .sel(in_2));  // open: en
  Multiplexer #(.width(32)) multiplexer_42 (
    .in0(multiplexer_14_out), .in1(help_me_24_out_3), .out(multiplexer_42_out), .sel(in_2));  // open: en
  Multiplexer #(.width(32)) multiplexer_43 (
    .in0(multiplexer_15_out), .in1(help_me_25_out_3), .out(multiplexer_43_out), .sel(in_2));  // open: en
  Multiplexer #(.width(32)) multiplexer_44 (
    .in0(multiplexer_16_out), .in1(help_me_26_out_3), .out(multiplexer_44_out), .sel(in_2));  // open: en
  Multiplexer #(.width(32)) multiplexer_45 (
    .in0(multiplexer_17_out), .in1(help_me_27_out_3), .out(multiplexer_45_out), .sel(in_2));  // open: en
  Multiplexer #(.width(32)) multiplexer_46 (
    .in0(multiplexer_18_out), .in1(help_me_28_out_3), .out(multiplexer_46_out), .sel(in_2));  // open: en
  help_me help_me_1 (.in_2({29{1'b0}}), .out_4(help_me_1_out_4), .vin({28{1'b0}}), .out_3(help_me_1_out_3));
  help_me help_me_2 (.in_2({29{1'b0}}), .out_4(help_me_2_out_4), .vin(28'h421e108), .out_3(help_me_2_out_3));
  help_me help_me_3 (.in_2({29{1'b0}}), .out_4(help_me_3_out_4), .vin(28'hc33f30c), .out_3(help_me_3_out_3));
  help_me help_me_4 (.in_2(29'hf0c223e), .out_4(help_me_4_out_4), .vin(28'hc373b0c), .out_3(help_me_4_out_3));
  help_me help_me_5 (.in_2(29'h1f9e367e), .out_4(help_me_5_out_4), .vin(28'hc361b0c), .out_3(help_me_5_out_3));
  help_me help_me_6 (.in_2(29'h18335d60), .out_4(help_me_6_out_4), .vin(28'he761b0c), .out_3(help_me_6_out_3));
  help_me help_me_7 (.in_2(29'h18334960), .out_4(help_me_7_out_4), .vin(28'h7e61b0c), .out_3(help_me_7_out_3));
  help_me help_me_8 (.in_2(29'h183f417e), .out_4(help_me_8_out_4), .vin(28'h3c61b0c), .out_3(help_me_8_out_3));
  help_me help_me_9 (.in_2(29'h1bbf637e), .out_4(help_me_9_out_4), .vin(28'h1861b0c), .out_3(help_me_9_out_3));
  help_me help_me_10 (.in_2(29'h1ab36360), .out_4(help_me_10_out_4), .vin(28'h1861b0c), .out_3(help_me_10_out_3));
  help_me help_me_11 (.in_2(29'h18b36360), .out_4(help_me_11_out_4), .vin(28'h1873b9c), .out_3(help_me_11_out_3));
  help_me help_me_12 (.in_2(29'h1fb3637e), .out_4(help_me_12_out_4), .vin(28'h183f1f8), .out_3(help_me_12_out_3));
  help_me help_me_13 (.in_2(29'hf12223e), .out_4(help_me_13_out_4), .vin(28'h181e0f0), .out_3(help_me_13_out_3));
  help_me help_me_14 (.in_2({29{1'b0}}), .out_4(help_me_14_out_4), .vin({28{1'b0}}), .out_3(help_me_14_out_3));
  help_me help_me_15 (.in_2({29{1'b0}}), .out_4(help_me_15_out_4), .vin({28{1'b0}}), .out_3(help_me_15_out_3));
  help_me help_me_16 (.in_2(29'h6209f3c), .out_4(help_me_16_out_4), .vin(28'h805fb0c), .out_3(help_me_16_out_3));
  help_me help_me_17 (.in_2(29'hf20bf66), .out_4(help_me_17_out_4), .vin(28'hc0dfb0c), .out_3(help_me_17_out_3));
  help_me help_me_18 (.in_2(29'h1fb1b062), .out_4(help_me_18_out_4), .vin(28'hc0c638c), .out_3(help_me_18_out_3));
  help_me help_me_19 (.in_2(29'h19b1b066), .out_4(help_me_19_out_4), .vin(28'hc0c638c), .out_3(help_me_19_out_3));
  help_me help_me_20 (.in_2(29'h19b1bf7c), .out_4(help_me_20_out_4), .vin(28'hc0c63cc), .out_3(help_me_20_out_3));
  help_me help_me_21 (.in_2(29'h199b3f70), .out_4(help_me_21_out_4), .vin(28'hc0c63ec), .out_3(help_me_21_out_3));
  help_me help_me_22 (.in_2(29'h199b3078), .out_4(help_me_22_out_4), .vin(28'hc0c63ec), .out_3(help_me_22_out_3));
  help_me help_me_23 (.in_2(29'h1f8e306c), .out_4(help_me_23_out_4), .vin(28'hccc637c), .out_3(help_me_23_out_3));
  help_me help_me_24 (.in_2(29'hf0e3f66), .out_4(help_me_24_out_4), .vin(28'hdec633c), .out_3(help_me_24_out_3));
  help_me help_me_25 (.in_2(29'h6041f62), .out_4(help_me_25_out_4), .vin(28'hf3c633c), .out_3(help_me_25_out_3));
  help_me help_me_26 (.in_2({29{1'b0}}), .out_4(help_me_26_out_4), .vin(28'he1dfb1c), .out_3(help_me_26_out_3));
  help_me help_me_27 (.in_2({29{1'b0}}), .out_4(help_me_27_out_4), .vin(28'h409fb18), .out_3(help_me_27_out_3));
  help_me help_me_28 (.in_2({29{1'b0}}), .out_4(help_me_28_out_4), .vin({28{1'b0}}), .out_3(help_me_28_out_3));
  Multiplexer #(.width(32)) multiplexer_47 (
    .in0(multiplexer_19_out), .in1(help_me_1_out_4), .out(out_23), .sel(in_3));  // open: en
  Multiplexer #(.width(32)) multiplexer_48 (
    .in0(multiplexer_20_out), .in1(help_me_2_out_4), .out(out_27), .sel(in_3));  // open: en
  Multiplexer #(.width(32)) multiplexer_49 (
    .in0(multiplexer_21_out), .in1(help_me_3_out_4), .out(out_31), .sel(in_3));  // open: en
  Multiplexer #(.width(32)) multiplexer_50 (
    .in0(multiplexer_22_out), .in1(help_me_4_out_4), .out(out_35), .sel(in_3));  // open: en
  Multiplexer #(.width(32)) multiplexer_51 (
    .in0(multiplexer_23_out), .in1(help_me_5_out_4), .out(out_39), .sel(in_3));  // open: en
  Multiplexer #(.width(32)) multiplexer_52 (
    .in0(multiplexer_24_out), .in1(help_me_6_out_4), .out(out_43), .sel(in_3));  // open: en
  Multiplexer #(.width(32)) multiplexer_53 (
    .in0(multiplexer_25_out), .in1(help_me_7_out_4), .out(out_47), .sel(in_3));  // open: en
  Multiplexer #(.width(32)) multiplexer_54 (
    .in0(multiplexer_26_out), .in1(help_me_8_out_4), .out(out_51), .sel(in_3));  // open: en
  Multiplexer #(.width(32)) multiplexer_55 (
    .in0(multiplexer_27_out), .in1(help_me_9_out_4), .out(out_55), .sel(in_3));  // open: en
  Multiplexer #(.width(32)) multiplexer_56 (
    .in0(multiplexer_28_out), .in1(help_me_10_out_4), .out(out_59), .sel(in_3));  // open: en
  Multiplexer #(.width(32)) multiplexer_57 (
    .in0(multiplexer_29_out), .in1(help_me_11_out_4), .out(out_63), .sel(in_3));  // open: en
  Multiplexer #(.width(32)) multiplexer_58 (
    .in0(multiplexer_30_out), .in1(help_me_12_out_4), .out(out_67), .sel(in_3));  // open: en
  Multiplexer #(.width(32)) multiplexer_59 (
    .in0(multiplexer_31_out), .in1(help_me_13_out_4), .out(out_71), .sel(in_3));  // open: en
  Multiplexer #(.width(32)) multiplexer_60 (
    .in0(multiplexer_32_out), .in1(help_me_14_out_4), .out(out_75), .sel(in_3));  // open: en
  Multiplexer #(.width(32)) multiplexer_61 (
    .in0(multiplexer_33_out), .in1(help_me_15_out_4), .out(out_79), .sel(in_3));  // open: en
  Multiplexer #(.width(32)) multiplexer_62 (
    .in0(multiplexer_34_out), .in1(help_me_16_out_4), .out(out_83), .sel(in_3));  // open: en
  Multiplexer #(.width(32)) multiplexer_63 (
    .in0(multiplexer_35_out), .in1(help_me_17_out_4), .out(out_87), .sel(in_3));  // open: en
  Multiplexer #(.width(32)) multiplexer_64 (
    .in0(multiplexer_36_out), .in1(help_me_18_out_4), .out(out_91), .sel(in_3));  // open: en
  Multiplexer #(.width(32)) multiplexer_65 (
    .in0(multiplexer_37_out), .in1(help_me_19_out_4), .out(out_95), .sel(in_3));  // open: en
  Multiplexer #(.width(32)) multiplexer_66 (
    .in0(multiplexer_38_out), .in1(help_me_20_out_4), .out(out_99), .sel(in_3));  // open: en
  Multiplexer #(.width(32)) multiplexer_67 (
    .in0(multiplexer_39_out), .in1(help_me_21_out_4), .out(out_103), .sel(in_3));  // open: en
  Multiplexer #(.width(32)) multiplexer_68 (
    .in0(multiplexer_40_out), .in1(help_me_22_out_4), .out(out_107), .sel(in_3));  // open: en
  Multiplexer #(.width(32)) multiplexer_69 (
    .in0(multiplexer_41_out), .in1(help_me_23_out_4), .out(out_111), .sel(in_3));  // open: en
  Multiplexer #(.width(32)) multiplexer_70 (
    .in0(multiplexer_42_out), .in1(help_me_24_out_4), .out(out_115), .sel(in_3));  // open: en
  Multiplexer #(.width(32)) multiplexer_71 (
    .in0(multiplexer_43_out), .in1(help_me_25_out_4), .out(out_119), .sel(in_3));  // open: en
  Multiplexer #(.width(32)) multiplexer_72 (
    .in0(multiplexer_44_out), .in1(help_me_26_out_4), .out(out_123), .sel(in_3));  // open: en
  Multiplexer #(.width(32)) multiplexer_73 (
    .in0(multiplexer_45_out), .in1(help_me_27_out_4), .out(out_127), .sel(in_3));  // open: en
  Multiplexer #(.width(32)) multiplexer_74 (
    .in0(multiplexer_46_out), .in1(help_me_28_out_4), .out(out_131), .sel(in_3));  // open: en
  Multiplexer #(.width(29)) multiplexer_75 (.in0({29{1'b0}}), .in1({29{1'b0}}), .out(out_20), .sel(in_3));  // open: en
  Multiplexer #(.width(29)) multiplexer_76 (.in0({29{1'b0}}), .in1({29{1'b0}}), .out(out_24), .sel(in_3));  // open: en
  Multiplexer #(.width(29)) multiplexer_77 (.in0({29{1'b0}}), .in1({29{1'b0}}), .out(out_28), .sel(in_3));  // open: en
  Multiplexer #(.width(29)) multiplexer_78 (.in0({29{1'b0}}), .in1({29{1'b0}}), .out(out_32), .sel(in_3));  // open: en
  Multiplexer #(.width(29)) multiplexer_79 (.in0({29{1'b0}}), .in1(29'hf0c223e), .out(out_36), .sel(in_3));  // open: en
  Multiplexer #(.width(29)) multiplexer_80 (
    .in0({29{1'b0}}), .in1(29'h1f9e367e), .out(out_40), .sel(in_3));  // open: en
  Multiplexer #(.width(29)) multiplexer_81 (
    .in0({29{1'b0}}), .in1(29'h18335d60), .out(out_44), .sel(in_3));  // open: en
  Multiplexer #(.width(29)) multiplexer_82 (
    .in0({29{1'b0}}), .in1(29'h18334960), .out(out_48), .sel(in_3));  // open: en
  Multiplexer #(.width(29)) multiplexer_83 (
    .in0({29{1'b0}}), .in1(29'h183f417e), .out(out_52), .sel(in_3));  // open: en
  Multiplexer #(.width(29)) multiplexer_84 (
    .in0({29{1'b0}}), .in1(29'h1bbf637e), .out(out_56), .sel(in_3));  // open: en
  Multiplexer #(.width(29)) multiplexer_85 (
    .in0({29{1'b0}}), .in1(29'h1ab36360), .out(out_60), .sel(in_3));  // open: en
  Multiplexer #(.width(29)) multiplexer_86 (
    .in0({29{1'b0}}), .in1(29'h18b36360), .out(out_64), .sel(in_3));  // open: en
  Multiplexer #(.width(29)) multiplexer_87 (
    .in0({29{1'b0}}), .in1(29'h1fb3637e), .out(out_68), .sel(in_3));  // open: en
  Multiplexer #(.width(29)) multiplexer_88 (.in0({29{1'b0}}), .in1(29'hf12223e), .out(out_72), .sel(in_3));  // open: en
  Multiplexer #(.width(29)) multiplexer_89 (.in0({29{1'b0}}), .in1({29{1'b0}}), .out(out_76), .sel(in_3));  // open: en
  Multiplexer #(.width(29)) multiplexer_90 (.in0({29{1'b0}}), .in1({29{1'b0}}), .out(out_80), .sel(in_3));  // open: en
  Multiplexer #(.width(29)) multiplexer_91 (.in0({29{1'b0}}), .in1(29'h6209f3c), .out(out_84), .sel(in_3));  // open: en
  Multiplexer #(.width(29)) multiplexer_92 (.in0({29{1'b0}}), .in1(29'hf20bf66), .out(out_88), .sel(in_3));  // open: en
  Multiplexer #(.width(29)) multiplexer_93 (
    .in0({29{1'b0}}), .in1(29'h1fb1b062), .out(out_92), .sel(in_3));  // open: en
  Multiplexer #(.width(29)) multiplexer_94 (
    .in0({29{1'b0}}), .in1(29'h19b1b066), .out(out_96), .sel(in_3));  // open: en
  Multiplexer #(.width(29)) multiplexer_95 (
    .in0({29{1'b0}}), .in1(29'h19b1bf7c), .out(out_100), .sel(in_3));  // open: en
  Multiplexer #(.width(29)) multiplexer_96 (
    .in0({29{1'b0}}), .in1(29'h199b3f70), .out(out_104), .sel(in_3));  // open: en
  Multiplexer #(.width(29)) multiplexer_97 (
    .in0({29{1'b0}}), .in1(29'h199b3078), .out(out_108), .sel(in_3));  // open: en
  Multiplexer #(.width(29)) multiplexer_98 (
    .in0({29{1'b0}}), .in1(29'h1f8e306c), .out(out_112), .sel(in_3));  // open: en
  Multiplexer #(.width(29)) multiplexer_99 (
    .in0({29{1'b0}}), .in1(29'hf0e3f66), .out(out_116), .sel(in_3));  // open: en
  Multiplexer #(.width(29)) multiplexer_100 (
    .in0({29{1'b0}}), .in1(29'h6041f62), .out(out_120), .sel(in_3));  // open: en
  Multiplexer #(.width(29)) multiplexer_101 (
    .in0({29{1'b0}}), .in1({29{1'b0}}), .out(out_124), .sel(in_3));  // open: en
  Multiplexer #(.width(29)) multiplexer_102 (
    .in0({29{1'b0}}), .in1({29{1'b0}}), .out(out_128), .sel(in_3));  // open: en
  Multiplexer #(.width(29)) multiplexer_103 (
    .in0({29{1'b0}}), .in1({29{1'b0}}), .out(out_132), .sel(in_3));  // open: en
  Multiplexer #(.width(29)) multiplexer_104 (
    .in0({29{1'b0}}), .in1({29{1'b0}}), .out(out_136), .sel(in_3));  // open: en
  Multiplexer #(.width(28)) multiplexer_105 (
    .in0({28{1'b0}}), .in1({28{1'b0}}), .out(out_21), .sel(in_2), .en(undriven));
  Multiplexer #(.width(28)) multiplexer_106 (.in0({28{1'b0}}), .in1({28{1'b0}}), .out(out_25), .sel(in_2));  // open: en
  Multiplexer #(.width(28)) multiplexer_107 (
    .in0({28{1'b0}}), .in1(28'h421e108), .out(out_29), .sel(in_2));  // open: en
  Multiplexer #(.width(28)) multiplexer_108 (
    .in0({28{1'b0}}), .in1(28'hc33f30c), .out(out_33), .sel(in_2));  // open: en
  Multiplexer #(.width(28)) multiplexer_109 (
    .in0({28{1'b0}}), .in1(28'hc373b0c), .out(out_37), .sel(in_2));  // open: en
  Multiplexer #(.width(28)) multiplexer_110 (
    .in0({28{1'b0}}), .in1(28'hc361b0c), .out(out_41), .sel(in_2));  // open: en
  Multiplexer #(.width(28)) multiplexer_111 (
    .in0({28{1'b0}}), .in1(28'he761b0c), .out(out_45), .sel(in_2));  // open: en
  Multiplexer #(.width(28)) multiplexer_112 (
    .in0({28{1'b0}}), .in1(28'h7e61b0c), .out(out_49), .sel(in_2));  // open: en
  Multiplexer #(.width(28)) multiplexer_113 (
    .in0({28{1'b0}}), .in1(28'h3c61b0c), .out(out_53), .sel(in_2));  // open: en
  Multiplexer #(.width(28)) multiplexer_114 (
    .in0({28{1'b0}}), .in1(28'h1861b0c), .out(out_57), .sel(in_2));  // open: en
  Multiplexer #(.width(28)) multiplexer_115 (
    .in0({28{1'b0}}), .in1(28'h1861b0c), .out(out_61), .sel(in_2));  // open: en
  Multiplexer #(.width(28)) multiplexer_116 (
    .in0({28{1'b0}}), .in1(28'h1873b9c), .out(out_65), .sel(in_2));  // open: en
  Multiplexer #(.width(28)) multiplexer_117 (
    .in0({28{1'b0}}), .in1(28'h183f1f8), .out(out_69), .sel(in_2));  // open: en
  Multiplexer #(.width(28)) multiplexer_118 (
    .in0({28{1'b0}}), .in1(28'h181e0f0), .out(out_73), .sel(in_2));  // open: en
  Multiplexer #(.width(28)) multiplexer_119 (.in0({28{1'b0}}), .in1({28{1'b0}}), .out(out_77), .sel(in_2));  // open: en
  Multiplexer #(.width(28)) multiplexer_120 (.in0({28{1'b0}}), .in1({28{1'b0}}), .out(out_81), .sel(in_2));  // open: en
  Multiplexer #(.width(28)) multiplexer_121 (
    .in0({28{1'b0}}), .in1(28'h805fb0c), .out(out_85), .sel(in_2));  // open: en
  Multiplexer #(.width(28)) multiplexer_122 (
    .in0({28{1'b0}}), .in1(28'hc0dfb0c), .out(out_89), .sel(in_2));  // open: en
  Multiplexer #(.width(28)) multiplexer_123 (
    .in0({28{1'b0}}), .in1(28'hc0c638c), .out(out_93), .sel(in_2));  // open: en
  Multiplexer #(.width(28)) multiplexer_124 (
    .in0({28{1'b0}}), .in1(28'hc0c638c), .out(out_97), .sel(in_2));  // open: en
  Multiplexer #(.width(28)) multiplexer_125 (
    .in0({28{1'b0}}), .in1(28'hc0c63cc), .out(out_101), .sel(in_2));  // open: en
  Multiplexer #(.width(28)) multiplexer_126 (
    .in0({28{1'b0}}), .in1(28'hc0c63ec), .out(out_105), .sel(in_2));  // open: en
  Multiplexer #(.width(28)) multiplexer_127 (
    .in0({28{1'b0}}), .in1(28'hc0c63ec), .out(out_109), .sel(in_2));  // open: en
  Multiplexer #(.width(28)) multiplexer_128 (
    .in0({28{1'b0}}), .in1(28'hccc637c), .out(out_113), .sel(in_2));  // open: en
  Multiplexer #(.width(28)) multiplexer_129 (
    .in0({28{1'b0}}), .in1(28'hdec633c), .out(out_117), .sel(in_2));  // open: en
  Multiplexer #(.width(28)) multiplexer_130 (
    .in0({28{1'b0}}), .in1(28'hf3c633c), .out(out_121), .sel(in_2));  // open: en
  Multiplexer #(.width(28)) multiplexer_131 (
    .in0({28{1'b0}}), .in1(28'he1dfb1c), .out(out_125), .sel(in_2));  // open: en
  Multiplexer #(.width(28)) multiplexer_132 (
    .in0({28{1'b0}}), .in1(28'h409fb18), .out(out_129), .sel(in_2));  // open: en
  Multiplexer #(.width(28)) multiplexer_133 (
    .in0({28{1'b0}}), .in1({28{1'b0}}), .out(out_133), .sel(in_2));  // open: en
  Multiplexer #(.width(28)) multiplexer_134 (
    .in0({28{1'b0}}), .in1({28{1'b0}}), .out(out_137), .sel(in_2));  // open: en
  Multiplexer #(.width(31)) multiplexer_135 (
    .in0({31{1'b0}}), .in1({31{1'b0}}), .out(multiplexer_135_out), .sel(vec_adr));  // open: en
  Multiplexer #(.width(31)) multiplexer_136 (
    .in0({31{1'b0}}), .in1({31{1'b0}}), .out(multiplexer_136_out), .sel(vec_adr));  // open: en
  Multiplexer #(.width(31)) multiplexer_137 (
    .in0({31{1'b0}}), .in1(31'h78), .out(multiplexer_137_out), .sel(vec_adr));  // open: en
  Multiplexer #(.width(31)) multiplexer_138 (
    .in0({31{1'b0}}), .in1(31'h78), .out(multiplexer_138_out), .sel(vec_adr));  // open: en
  Multiplexer #(.width(31)) multiplexer_139 (
    .in0({31{1'b0}}), .in1(31'h78), .out(multiplexer_139_out), .sel(vec_adr));  // open: en
  Multiplexer #(.width(31)) multiplexer_140 (
    .in0({31{1'b0}}), .in1(31'h78), .out(multiplexer_140_out), .sel(vec_adr));  // open: en
  Multiplexer #(.width(31)) multiplexer_141 (
    .in0({31{1'b0}}), .in1(31'h78), .out(multiplexer_141_out), .sel(vec_adr));  // open: en
  Multiplexer #(.width(31)) multiplexer_142 (
    .in0({31{1'b0}}), .in1({31{1'b0}}), .out(multiplexer_142_out), .sel(vec_adr));  // open: en
  Multiplexer #(.width(31)) multiplexer_143 (
    .in0({31{1'b0}}), .in1({31{1'b0}}), .out(multiplexer_143_out), .sel(vec_adr));  // open: en
  Multiplexer #(.width(31)) multiplexer_144 (
    .in0(multiplexer_135_out), .in1({31{1'b0}}), .out(out_66), .sel(key));  // open: en
  Multiplexer #(.width(31)) multiplexer_145 (
    .in0(multiplexer_136_out), .in1({31{1'b0}}), .out(out_70), .sel(key));  // open: en
  Multiplexer #(.width(31)) multiplexer_146 (
    .in0(multiplexer_137_out), .in1(31'h384), .out(out_74), .sel(key));  // open: en
  Multiplexer #(.width(31)) multiplexer_147 (
    .in0(multiplexer_138_out), .in1(31'h6d4), .out(out_78), .sel(key));  // open: en
  Multiplexer #(.width(31)) multiplexer_148 (
    .in0(multiplexer_139_out), .in1(31'h47c), .out(out_82), .sel(key));  // open: en
  Multiplexer #(.width(31)) multiplexer_149 (
    .in0(multiplexer_140_out), .in1(31'h6c0), .out(out_86), .sel(key));  // open: en
  Multiplexer #(.width(31)) multiplexer_150 (
    .in0(multiplexer_141_out), .in1(31'h380), .out(out_90), .sel(key));  // open: en
  Multiplexer #(.width(31)) multiplexer_151 (
    .in0(multiplexer_142_out), .in1({31{1'b0}}), .out(out_94), .sel(key));  // open: en
  Multiplexer #(.width(31)) multiplexer_152 (
    .in0(multiplexer_143_out), .in1({31{1'b0}}), .out(out_98), .sel(key));  // open: en

  assign out_18 = {32{1'b1}};
  assign out_19 = {32{1'b1}};
  assign out_22 = {31{1'b0}};
  assign out_26 = {31{1'b0}};
  assign out_30 = {31{1'b0}};
  assign out_34 = {31{1'b0}};
  assign out_38 = {31{1'b0}};
  assign out_42 = {31{1'b0}};
  assign out_46 = {31{1'b0}};
  assign out_50 = {31{1'b0}};
  assign out_54 = {31{1'b0}};
  assign out_58 = {31{1'b0}};
  assign out_62 = {31{1'b0}};
  assign out_102 = {31{1'b0}};
  assign out_106 = {31{1'b0}};
  assign out_110 = {31{1'b0}};
  assign out_114 = {31{1'b0}};
  assign out_118 = {31{1'b0}};
  assign out_122 = {31{1'b0}};
  assign out_126 = {31{1'b0}};
  assign out_130 = {31{1'b0}};
  assign out_134 = {31{1'b0}};
  assign out_135 = {32{1'b1}};
  assign out_138 = {31{1'b0}};
  assign out_139 = {32{1'b1}};
  assign out_140 = {31{1'b0}};

  // Other names for the same wires on the sheet: d = in_4; k = in_5; lose = in_3; win = in_2

  // Notes on the sheet:
  //   1
  //   2
  //   3
  //   4
  //   5
  //   6
  //   7
  //   8
  //   9
  //   10
  //   11
  //   12
  //   13
  //   14
  //   15
  //   16
  //   17
  //   18
  //   19
  //   20
  //   21
  //   22
  //   23
  //   24
  //   25
  //   26
  //   27
  //   28
  //   29
  //   30
  //   1
  //   2
  //   3
  //   4
  //   5
  //   6
  //   7
  //   8
  //   9
  //   10
  //   11
  //   12
  //   13
  //   14
  //   15
  //   16
  //   17
  //   18
  //   19
  //   20
  //   21
  //   22
  //   23
  //   24
  //   25
  //   26
  //   27
  //   28
  //   29
  //   30
  //   1
  //   2
  //   3
  //   4
  //   5
  //   6
  //   7
  //   8
  //   9
  //   10
  //   11
  //   21
  //   22
  //   23
  //   24
  //   25
  //   26
  //   27
  //   28
  //   29
  //   30
  //   31
  //   12
  //   14
  //   15
  //   16
  //   17
  //   13
  //   18
  //   19
  //   20
endmodule

module tunnel_for_display (
  input  [28:0] in_1,
  input  [28:0] in_2,
  input  [28:0] in_3,
  input  [28:0] in_4,
  input  [28:0] in_5,
  input  [28:0] in_6,
  input  [28:0] in_7,
  input  [28:0] in_8,
  input  [28:0] in_9,
  input  [28:0] in_10,
  input  [28:0] in_11,
  input  [28:0] in_12,
  input  [28:0] in_13,
  input  [28:0] in_14,
  input  [28:0] in_15,
  input  [28:0] in_16,
  input  [28:0] in_17,
  input  [28:0] in_18,
  input  [28:0] in_19,
  input  [28:0] in_20,
  input  [28:0] in_21,
  input  [28:0] in_22,
  input  [28:0] in_23,
  input  [28:0] in_24,
  input  [28:0] in_25,
  input  [28:0] in_26,
  input  [28:0] in_27,
  input  [28:0] in_28,
  input  [28:0] in_29,
  input  [28:0] in_30,
  output [28:0] out_31,
  output [28:0] out_32,
  output [28:0] out_33,
  output [28:0] out_34,
  output [28:0] out_35,
  output [28:0] out_36,
  output [28:0] out_37,
  output [28:0] out_38,
  output [28:0] out_39,
  output [28:0] out_40,
  output [28:0] out_41,
  output [28:0] out_42,
  output [28:0] out_43,
  output [28:0] out_44,
  output [28:0] out_45,
  output [28:0] out_46,
  output [28:0] out_47,
  output [28:0] out_48,
  output [28:0] out_49,
  output [28:0] out_50,
  output [28:0] out_51,
  output [28:0] out_52,
  output [28:0] out_53,
  output [28:0] out_54,
  output [28:0] out_55,
  output [28:0] out_56,
  output [28:0] out_57,
  output [28:0] out_58,
  output [28:0] out_59,
  output [28:0] out_60
);


  assign out_31 = in_1;
  assign out_32 = in_2;
  assign out_33 = in_3;
  assign out_34 = in_4;
  assign out_35 = in_5;
  assign out_36 = in_6;
  assign out_37 = in_7;
  assign out_38 = in_8;
  assign out_39 = in_9;
  assign out_40 = in_10;
  assign out_41 = in_11;
  assign out_42 = in_12;
  assign out_43 = in_13;
  assign out_44 = in_14;
  assign out_45 = in_15;
  assign out_46 = in_16;
  assign out_47 = in_17;
  assign out_48 = in_18;
  assign out_49 = in_19;
  assign out_50 = in_20;
  assign out_51 = in_21;
  assign out_52 = in_22;
  assign out_53 = in_23;
  assign out_54 = in_24;
  assign out_55 = in_25;
  assign out_56 = in_26;
  assign out_57 = in_27;
  assign out_58 = in_28;
  assign out_59 = in_29;
  assign out_60 = in_30;
endmodule

module CP (
  input  [6:0] Name,
  input  [7:0] Score,
  input  in_3,
  output [6:0] ASKII
);

  wire button_1_out, button_2_out, cdm_8_1_p9, cdm_8_1_p10, clock, comparator_1_eq, comparator_2_eq,
       comparator_3_eq, controlled_buffer_1_out, multiplexer_3_out, multiplexer_4_out, multiplexer_5_out,
       not_1_out, not_2_out, not_3_out, not_4_out, or_1_out, write;
  wire [6:0] register_1_q, xor_1_out;
  wire [7:0] bit_extender_1_out, cdm_8_1_p11, cdm_8_1_p12, cdm_8_1_p13, controlled_buffer_2_out,
       controlled_buffer_4_out, controlled_buffer_5_out, controlled_buffer_7_out, counter_1_q, input_count,
       multiplexer_1_out, multiplexer_2_out, multiplexer_6_out, rom_1_data, rom_2_data;

  Register #(.width(7)) register_1 (.D(Name), .Q(register_1_q), .clk(clock));  // open: en, clr
  Button button_1 (.out(button_1_out));
  assign controlled_buffer_1_out = in_3 ? clock : 1'bz;  // Controlled_Buffer controlled_buffer_1
  Clock clock_1 (.out(clock));
  // Probe on xor_1_out
  assign xor_1_out = register_1_q ^ Name;  // XOR_Gate xor_1, 7 bits wide
  Counter counter_1 (.count(clock), .Q(counter_1_q), .clk(clock), .clr(not_1_out));  // open: load, D, carry
  not not_1 (not_1_out, write);
  Counter counter_2 (.count(or_1_out), .Q(input_count), .clk(clock));  // open: load, D, carry, clr
  or or_1 (or_1_out, xor_1_out[0], xor_1_out[1], xor_1_out[2], xor_1_out[3], xor_1_out[4], xor_1_out[5], xor_1_out[6]);
  // Probe on counter_1_q
  // Probe on cdm_8_1_p11
  // CdM_8 cdm_8_1: pin names not known; wires that end beside it: controlled_buffer_1_out, {8{1'b0}}, button_1_out, {8{1'b0}}, {8{1'b0}}, {8{1'b0}}, {8{1'b0}}, {8{1'b0}}, cdm_8_1_p9, cdm_8_1_p10, cdm_8_1_p11, cdm_8_1_p12, cdm_8_1_p13
  assign controlled_buffer_2_out = not_2_out ? cdm_8_1_p12 : 8'bz;  // Controlled_Buffer controlled_buffer_2
  not not_2 (not_2_out, cdm_8_1_p10);
  assign cdm_8_1_p13 = cdm_8_1_p10 ? controlled_buffer_4_out : 8'bz;  // Controlled_Buffer controlled_buffer_3
  ROM rom_1 (.addr(input_count), .data(rom_1_data));  // open: sel
  Multiplexer #(.width(8), .enable("false")) multiplexer_1 (
    .in0(rom_1_data), .in1(cdm_8_1_p11), .out(multiplexer_1_out), .sel(in_3));
  Multiplexer #(.width(8), .enable("false")) multiplexer_2 (
    .in0(multiplexer_1_out), .in1(rom_2_data), .out(multiplexer_2_out), .sel(write));
  ROM rom_2 (.addr(counter_1_q), .data(rom_2_data));  // open: sel
  // Probe on rom_2_data
  not not_3 (not_3_out, write);
  assign controlled_buffer_4_out = not_3_out ? controlled_buffer_5_out : 8'bz;  // Controlled_Buffer controlled_buffer_4
  Comparator comparator_1 (.a(rom_2_data), .b({8{1'b0}}), .eq(comparator_1_eq));  // open: gt, lt
  Multiplexer #(.enable("false")) multiplexer_3 (.in0(cdm_8_1_p9), .in1(1'b1), .out(multiplexer_3_out), .sel(write));
  Multiplexer #(.enable("false")) multiplexer_4 (
    .in0(multiplexer_5_out), .in1(1'b1), .out(multiplexer_4_out), .sel(write));
  Multiplexer #(.enable("false")) multiplexer_5 (.in0(1'b0), .in1(cdm_8_1_p10), .out(multiplexer_5_out), .sel(in_3));
  assign controlled_buffer_5_out = not_3_out ? controlled_buffer_2_out : 8'bz;  // Controlled_Buffer controlled_buffer_5
  // Probe on controlled_buffer_5_out
  RAM ram_1 (
    .addr(multiplexer_2_out), .data(controlled_buffer_5_out), .sel(multiplexer_3_out), .clk(clock),
    .ld(multiplexer_4_out));  // open: clr
  assign bit_extender_1_out = {{1{1'b0}}, Name};  // Bit_Extender bit_extender_1
  Comparator comparator_2 (.a(input_count), .b(8'h1), .eq(comparator_2_eq));  // open: gt, lt
  Multiplexer #(.width(8), .enable("false")) multiplexer_6 (
    .in0(bit_extender_1_out), .in1(Score), .out(multiplexer_6_out), .sel(comparator_2_eq));
  not not_4 (not_4_out, in_3);
  assign controlled_buffer_5_out = not_4_out ? multiplexer_6_out : 8'bz;  // Controlled_Buffer controlled_buffer_6
  // Probe on controlled_buffer_5_out
  assign controlled_buffer_7_out = write ? controlled_buffer_5_out : 8'bz;  // Controlled_Buffer controlled_buffer_7
  // Probe on controlled_buffer_7_out
  Counter #(.width(1), .max('h1)) counter_3 (
    .count(comparator_3_eq), .Q(write), .clk(comparator_3_eq), .clr(comparator_1_eq));  // open: load, D, carry
  Comparator comparator_3 (.a(controlled_buffer_5_out), .b(8'hd4), .eq(comparator_3_eq));  // open: gt, lt
  Bit_Extender #(.out_width(7)) bit_extender_2 (.in(controlled_buffer_7_out), .out(ASKII));
  // Probe on ASKII
  TTY #(.rows(32), .cols(5)) tty_1 (.data(ASKII), .clk(clock), .we(write), .clr(button_2_out));
  Button button_2 (.out(button_2_out));

  // Other names for the same wires on the sheet: win = in_3

  // Notes on the sheet:
  //   contents of rom_1 (hex, n*v repeats v):
  //   86 87 88 89 8a 8b 8c 8d 8e 8f 90 91 92 93 94 95 96 97 98 99 9a 9b 9c 9d 9e 9f a0 a1 a2 a3
  //   contents of rom_2 (hex, n*v repeats v):
  //   86 87 88 89 8a 8b 8c 8d 8e 8f 90 91 92 93 94 95 96 97 98 99 9a 9b 9c 9d 9e 9f a0 a1 a2 a3
endmodule

module help_me (
  input  [27:0] vin,
  input  [28:0] in_2,
  output [31:0] out_3,
  output [31:0] out_4
);

  assign out_3[29:2] = ~vin;  // NOT_Gate not_1, 28 bits wide
  assign out_4[30:2] = ~in_2;  // NOT_Gate not_2, 29 bits wide

  assign {out_3[31:30], out_3[1:0]} = 4'b1111;
  assign {out_4[31], out_4[1:0]} = 3'b111;
endmodule
